# Fritzing sketch BT_sshble232fzz (saved by Fritzing 0.9.3b)
breadboards: 1

parts:
  Raspberry_Pi_1 = Raspberry Pi 3 [part_number=RPI-3-V1.2]
  U1 = SUP500F [package=sup500f]  # not connected
  Part2 = Bluetooth HC-05 Macho
  U2 = RELAY [package=relay-jzc]
  Power_plug1 = Power plug  # not connected

nets:
  N1: Raspberry_Pi_1.GIPO21, U2.MAIN
  N2: Raspberry_Pi_1.GIPO20, Part2.TXD
  N3: Raspberry_Pi_1.GIPO16, Part2.RXD
  GND: Raspberry_Pi_1.GND, Part2.GND, U2.COIL1
  5V: Raspberry_Pi_1.5V, Part2.VCC

notes:
  external bluetooth is optional for an increase in bluetooth range/can be breakout module or usb dongle
  gps data logged with python and gpsd, provides independent time and date via pps (pulse per second) signal from satelites
  A test event is logged when GPIO pin is driven high, can be activated via software script
  a Bluetooth Low Energy server hosted on the Raspberry Pi can receive commands from another BLE compatible device eg iphone or android
  A command can be sent to the Raspberry Pi via SSH(Secure Shell) over Bluetooth connection
  A virtual serial port can be created to send and receive messages. (Bluetooth Serial Port Profile)
  An application on the same wired or wireless netwok can send commands via http request
  The Raspberry Pi can host a wireless access point and have clients connect to it, this would not give internet connectivity to the RPI or connected client
  TEST ON / OFF
  Raspberry Pi models with in built bluetooth:
  RPI-0W Bluetooth 4.0
  RPI-3B Bluetooth 4.0
  RPI-3B+ Bluetooth 4.0
  RPI-3A+ Bluetooth 4.0
  RPI-4B - Bluetooth 5.0
  RPI4 Compute Module Bluetooth 5.0
  Recommended is the latest model Raspberry Pi 4B
  Software will work on all above models as long as an untouched and up to date vesion of Raspbian Lite or Raspbian Full isi used as base.
  Power Requirements
  RPI-4B 5.1v 3.0a
  RPI-3B+ 5.1v 2.5a
  RPI-3B 5.1v 2.1a
  RPI can be powered via micro usb pr usb-c
  depending on model.
  RPI can be also be powered by 5.1v to GPIO board pins 2 or 4 , this method
  by passes the onboard fusing.
  RPI GPIO pins work on 3.3v and will fail if 5v is connected to a 3.3v pin
